# Fritzing sketch RemotePower (saved by Fritzing 0.8.7b)
circuit board: 8.46667cm x 5.64444cm
breadboards: 1

parts:
  MICRO_USB_POWER = USB_MICROB_PLUG [package=micro-b-th]
  LD33 = V_REG_LD1117VXX [package=78xxl]
  AT328 = atmega328 [package=dip]
  CON_USBASP = AVR 10-pin ICSP Header [package=avr_icsp]
  JP_RELAY = Header 6 [package=molex-1x6-ra]
  J1 = female pin header, 2 pins [form="♀ (female)"]
  J2 = female pin header, 2 pins [form="♀ (female)"]
  J3 = female pin header, 2 pins [form="♀ (female)"]
  J4 = female pin header, 2 pins [form="♀ (female)"]

nets:
  VCC: MICRO_USB_POWER.VCC, LD33.IN, AT328.VCC, AT328.AVCC, AT328.AREF, CON_USBASP.2, JP_RELAY.1
  GND: MICRO_USB_POWER.GND, AT328.GND, CON_USBASP.10, JP_RELAY.6, J2.pin2
  N1: AT328.RESET, CON_USBASP.5
  N2: AT328.D0_(RX), CON_USBASP.6
  N3: AT328.D1_(TX), CON_USBASP.4
  N4: AT328.D2, J3.pin1
  N5: AT328.D3_(PWM), JP_RELAY.5
  N6: AT328.D4, JP_RELAY.4
  N7: AT328.D5_(PWM), JP_RELAY.3
  N8: AT328.D6_(PWM), JP_RELAY.2
  N9: AT328.D9_(PWM), J1.pin2
  N10: AT328.D10_(PWM), J1.pin1
  N11: AT328.D11_(PWM), CON_USBASP.1, J4.pin1
  N12: AT328.D12, CON_USBASP.9, J3.pin2
  N13: AT328.D13, CON_USBASP.7, J4.pin2
