# Fritzing sketch HomeAtion_main (saved by Fritzing 0.8.7b)
breadboards: 1

parts:
  AT328 = atmega328 [package=dip]
  J5 = Generic female header - 2 pins [form="♀ (female)" package=THT]
  J6 = Generic female header - 2 pins [form="♀ (female)" package=THT]
  J7 = Generic female header - 2 pins [form="♀ (female)" package=THT]
  J8 = Generic female header - 2 pins [form="♀ (female)" package=THT]
  Ethernet_Module = Generic shrouded header - 12 pins [form="♂ (shrouded male)" package=THT]
  S1 = Pushbutton [package="[THT]"]
  LDO_3_3V = V_REG_LD1117VXX [package=78xxl]
  C1 = Ceramic Capacitor [capacitance=100nF package="100 mil [THT, multilayer]"]
  C2 = Electrolytic Capacitor [capacitance=2.2µF package="100 mil [THT, electrolytic]"]
  JP1 = USB_MICROB_PLUG [package=micro-b-th]

nets:
  N1: AT328.RESET, S1.Pin_1, S1.Pin_2
  VCC: AT328.VCC, AT328.AVCC, AT328.AREF, Ethernet_Module.3.3V, LDO_3_3V.IN, C1.0, JP1.VCC
  GND: AT328.GND, J5.GND, Ethernet_Module.GND, S1.Pin_3, S1.Pin_4, LDO_3_3V.GND, C1.1, C2.-, JP1.GND
  N2: AT328.D7, J5.CE
  N3: AT328.D8, J7.CSN
  N4: AT328.D10_(PWM), Ethernet_Module.CS
  N5: AT328.D11_(PWM), J8.MOSI, Ethernet_Module.MOSI
  N6: AT328.D12, J6.MISO, Ethernet_Module.MISO
  N7: AT328.D13, J6.SCK, Ethernet_Module.SCK
  N8: J7.VCC, LDO_3_3V.OUT, C2.+

custom parts:
  Generic female header - 2 pins: Generic female header
  Generic female header - 2 pins: Generic female header
  Generic female header - 2 pins: Generic female header
  Generic female header - 2 pins: Generic female header
  Generic shrouded header - 12 pins: Generic shrouded header
  V_REG_LD1117VXX: LD1117VXX voltage regulator. We carry the 3.3V version (COM-00526) in TO-220 package.
