# Fritzing sketch HomeAtion_ClientBase_Breadboard (saved by Fritzing 0.9.2b)
breadboards: 1

parts:
  AT328 = atmega328 [package=dip]
  C1 = Ceramic Capacitor [capacitance=100nF package="100 mil [THT, multilayer]"]
  C2 = Electrolytic Capacitor [capacitance=2.2µF package="100 mil [THT, electrolytic]"]
  C3 = Ceramic Capacitor [capacitance=100nF package="100 mil [THT, multilayer]"]
  S2 = Pushbutton [package="[THT]"]
  R2 = Resistor [tolerance=±5% resistance=4.7k package=THT]
  LDO_3_3V1 = V_REG_LD1117VXX [package=78xxl]
  C4 = Electrolytic Capacitor [capacitance=2.2µF package="100 mil [THT, electrolytic]"]
  C5 = Ceramic Capacitor [capacitance=100nF package="100 mil [THT, multilayer]"]
  LED2 = LED - 5mm [color="Red (633nm)" package="5 mm [THT]"]
  R3 = Resistor [tolerance=±5% resistance=1k package=THT]
  J3 = female pin header, 4 pins [form="♀ (female)"]
  J2 = female pin header, 4 pins [form="♀ (female)"]
  J9 = male pin header, 5 pins [form="♂ (male)"]

nets:
  N1: AT328.RESET, S2.Pin_1, S2.Pin_2, R2.Pin_0
  N2: AT328.VCC, AT328.AVCC, C1.0, C2.+, C3.1, R2.Pin_1, LDO_3_3V1.IN, C5.0, J9.pin1
  GND: AT328.GND, C1.1, C2.-, S2.Pin_3, S2.Pin_4, LDO_3_3V1.GND, C4.-, C5.1, R3.Pin_1, J3.pin4, J9.pin5
  N3: AT328.D9_(PWM), J3.pin3
  N4: AT328.D10_(PWM), J2.pin3
  N5: AT328.D11_(PWM), J2.pin2
  N6: AT328.D12, J3.pin1
  N7: AT328.D13, J3.pin2
  N8: LDO_3_3V1.OUT, C4.+, J2.pin4
  N9: LED2.cathode, R3.Pin_0

custom parts:
  V_REG_LD1117VXX: LD1117VXX voltage regulator. We carry the 3.3V version (COM-00526) in TO-220 package.
