# Fritzing sketch HomeAtion_main (saved by Fritzing 0.8.7b)
circuit board: 8.46667cm x 5.64444cm
breadboards: 1

parts:
  AT328 = atmega328 [package=dip]
  LDO_3_3V = V_REG_LD1117VXX [package=78xxl]
  C1 = Ceramic Capacitor [capacitance=100nF package="100 mil [THT, multilayer]"]
  C2 = Electrolytic Capacitor [capacitance=2.2µF package="100 mil [THT, electrolytic]"]
  C4 = Electrolytic Capacitor [capacitance=2.2µF package="100 mil [THT, electrolytic]"]
  C3 = Ceramic Capacitor [capacitance=100nF package="100 mil [THT, multilayer]"]
  C5 = Ceramic Capacitor [capacitance=100nF package="100 mil [THT, multilayer]"]
  S1 = Pushbutton [package="[THT]"]
  R1 = Resistor [tolerance=±5% resistance=4.7k package=THT]
  SW1 = DIP SWITCH [package=dipswitch-02]
  LED1 = LED - 5mm [color="Red (633nm)" package="5 mm [THT]"]
  R2 = Resistor [tolerance=±5% resistance=1k package=THT]
  LED2 = RGB LED - (4 legs) [package="5 mm [THT]"]
  Ethernet_Module = shrouded pin header, 6 pins [form="♂ (shrouded male)"]
  J3 = double row female pin header, 4 pins [form="♀ (female)"]
  J2 = double row female pin header, 4 pins [form="♀ (female)"]
  R3 = Resistor [tolerance=±5% resistance=470 package=THT]
  R4 = Resistor [tolerance=±5% resistance=470 package=THT]
  R5 = Resistor [tolerance=±5% resistance=470 package=THT]
  J1 = male pin header, 5 pins [form="♂ (male)"]

nets:
  N1: AT328.RESET, S1.Pin_1, S1.Pin_2, R1.Pin_0
  N2: AT328.D3_(PWM), R3.Pin_0
  N3: AT328.VCC, AT328.AVCC, LDO_3_3V.IN, C1.0, C4.+, C3.0, C5.1, R1.Pin_1, SW1.4, LED1.anode, LED2.common_anode, Ethernet_Module.pin6
  GND: AT328.GND, LDO_3_3V.GND, C1.1, C2.-, C4.-, C3.1, C5.0, S1.Pin_3, S1.Pin_4, R2.Pin_1, Ethernet_Module.pin1, J3.pin4, J1.pin5
  N4: AT328.D5_(PWM), R4.Pin_0
  N5: AT328.D6_(PWM), R5.Pin_0
  N6: AT328.D7, J3.pin3
  N7: AT328.D8, J2.pin3
  N8: AT328.D10_(PWM), Ethernet_Module.pin5
  N9: AT328.D11_(PWM), Ethernet_Module.pin4, J2.pin2
  N10: AT328.D12, Ethernet_Module.pin3, J3.pin1
  N11: AT328.D13, Ethernet_Module.pin2, J3.pin2
  N12: LDO_3_3V.OUT, C2.+, SW1.3
  N13: SW1.1, J1.pin1
  N14: SW1.2, J2.pin4
  N15: LED1.cathode, R2.Pin_0
  N16: LED2.red_cathode, R3.Pin_1
  N17: LED2.green_cathode, R4.Pin_1
  N18: LED2.blue_cathode, R5.Pin_1

custom parts:
  V_REG_LD1117VXX: LD1117VXX voltage regulator. We carry the 3.3V version (COM-00526) in TO-220 package.
