# Fritzing sketch homeation_remoteleddhtbuzz_schematic (saved by Fritzing 0.8.7b)
breadboards: 1
perfboards: 1

parts:
  AT328 = atmega328 [package=dip]
  C1 = Ceramic Capacitor [capacitance=100nF package="100 mil [THT, multilayer]"]
  C2 = Electrolytic Capacitor [capacitance=2.2µF package="100 mil [THT, electrolytic]"]
  C3 = Ceramic Capacitor [capacitance=100nF package="100 mil [THT, multilayer]"]
  RESET = Pushbutton [package="[THT]"]
  R1 = Resistor [tolerance=±5% resistance=4.7k package=THT]
  LDO_3_3V = V_REG_LD1117VXX [package=78xxl]
  C4 = Electrolytic Capacitor [capacitance=2.2µF package="100 mil [THT, electrolytic]"]
  C5 = Ceramic Capacitor [capacitance=100nF package="100 mil [THT, multilayer]"]
  Main_switch = DIP SWITCH [package=dipswitch-02]
  R2 = Resistor [tolerance=±5% resistance=1k package=THT]
  Ethernet_module = shrouded pin header, 6 pins [form="♂ (shrouded male)"]
  NRF24 = double row female pin header, 8 pins [form="♀ (female)"]
  LED_Power = LED - 3mm [color="Red (633nm)" package="3 mm [THT]"]
  LED2 = LED - 3mm [color="Green (560nm)" package="3 mm [THT]"]
  R3 = Resistor [tolerance=±5% resistance=1k package=THT]

nets:
  5V: AT328.RESET, AT328.VCC, AT328.AVCC, C2.+, C3.1, RESET.Pin_1, RESET.Pin_2, R1.Pin_0, R1.Pin_1, Main_switch.2, Ethernet_module.pin6
  N1: AT328.D3_(PWM), LED2.anode
  GND: AT328.GND#7, C1.1, C2.-, RESET.Pin_3, RESET.Pin_4, LDO_3_3V.GND, C4.-, C5.1, R2.Pin_1, Ethernet_module.pin1, NRF24.pin1, R3.Pin_0
  N2: AT328.D9_(PWM), NRF24.pin3
  N3: AT328.D10_(PWM), NRF24.pin4
  N4: AT328.D11_(PWM), Ethernet_module.pin2, NRF24.pin6
  N5: AT328.D12, Ethernet_module.pin3, NRF24.pin7
  N6: AT328.D13, Ethernet_module.pin4, NRF24.pin5
  N7: AT328.GND#21, C3.0
  N8: AT328.A4, Ethernet_module.pin5
  Power3V3: LDO_3_3V.OUT, C4.+, Main_switch.4
  Power5V: LDO_3_3V.IN, C5.0, Main_switch.3, LED_Power.anode
  3.3V: Main_switch.1, NRF24.pin2
  N9: R2.Pin_0, LED_Power.cathode
  N10: LED2.cathode, R3.Pin_1

custom parts:
  V_REG_LD1117VXX: LD1117VXX voltage regulator. We carry the 3.3V version (COM-00526) in TO-220 package.
