# Fritzing sketch HomeAtion_RemoteLedEnv (saved by Fritzing 0.9.2b)
perfboards: 1

parts:
  ProMini = Arduino Pro Mini v13
  Power5V = Generic male header - 5 pins [form="♂ (male)" package=THT]
  Nrf24L01_2 = female pin header, 4 pins [form="♀ (female)"]
  Nrf24L01_1 = female pin header, 4 pins [form="♀ (female)"]
  Leds = female pin header, 3 pins [form="♀ (female)"]  # not connected
  NoiseSensor = female pin header, 3 pins [form="♀ (female)"]
  EnvSensor = female pin header, 3 pins [form="♀ (female)"]
  DEBUG = female pin header, 2 pins [form="♀ (female)"]
  TwoButtons = female pin header, 3 pins [form="♀ (female)"]
  R1 = Resistor [tolerance=±5% resistance=10k package=THT]
  R2 = Resistor [tolerance=±5% resistance=10k package=THT]

nets:
  3.3V: ProMini.VCC, Nrf24L01_1.pin4
  GND: ProMini.GND, Power5V.GND
  5V: ProMini.RAW, Power5V.VCC
  N1: ProMini.A1, Nrf24L01_2.pin1
  N2: ProMini.D12/MISO, Nrf24L01_1.pin2
  N3: ProMini.D10_PWM/SS, Nrf24L01_1.pin3
  N4: ProMini.D8, TwoButtons.pin2, R2.Pin_0
  N5: ProMini.D7, TwoButtons.pin3, R1.Pin_0
  N6: ProMini.D4, EnvSensor.pin2
  N7: ProMini.D1/RX, DEBUG.pin1
  N8: ProMini.D0/TX, DEBUG.pin2
  N9: NoiseSensor.pin3, EnvSensor.pin3, TwoButtons.pin1
  N10: EnvSensor.pin1, R1.Pin_1, R2.Pin_1

custom parts:
  Generic male header - 5 pins: Generic male header
