# Fritzing sketch HomeAtion_RemoteLedEnv_Breadboard_Schematic (saved by Fritzing 0.9.2b)

parts:
  ProMini = Arduino Pro Mini v13
  NRF24L01 = NRF24L01
  EnvSensor = DHT11 Humitidy and Temperature Sensor
  NoiseSensor = Breakout Board for Electret Microphone
  Leds = ws2812b [package="smd 2812b"]
  Power5V = Generic male header - 5 pins [form="♂ (male)" package=THT]
  S1 = Pushbutton [package=THT]
  S2 = Pushbutton [package=THT]
  R1 = Resistor [tolerance=±5% resistance=10k package=THT]
  R2 = Resistor [tolerance=±5% resistance=10k package=THT]

nets:
  3.3V: ProMini.VCC, NRF24L01.VCC, EnvSensor.VDD, NoiseSensor.VCC, S1.leg1, S2.leg1
  GND: ProMini.GND, NRF24L01.GND, EnvSensor.GND, NoiseSensor.GND, Leds.VSS, Power5V.GND, R1.Pin_0, R2.Pin_0
  5V: ProMini.RAW, Leds.VDD, Power5V.VCC
  N1: ProMini.A1, NoiseSensor.OUT
  N2: ProMini.D13/SCK, NRF24L01.SCK
  N3: ProMini.D12/MISO, NRF24L01.MISO
  N4: ProMini.D11_PWM/MOSI, NRF24L01.MOSI
  N5: ProMini.D10_PWM/SS, NRF24L01.CSN
  N6: ProMini.D9_PWM, NRF24L01.CE
  N7: ProMini.D8, S2.leg0, R2.Pin_1
  N8: ProMini.D7, S1.leg0, R1.Pin_1
  N9: ProMini.D4, EnvSensor.DATA
  N10: ProMini.D3_PWM, Leds.DIN

custom parts:
  NRF24L01: NRF24L01 module
  DHT11 Humitidy and Temperature Sensor: DHT11 Humidity and Temperature Sensor
  Breakout Board for Electret Microphone: Description: Ready to add audio to your next project? This small breakout board couples a small electret microphone with a 100x opamp to amplify the sounds of voice, door knocks, etc loud enough to be picked up by a microcontroller's Analog to Digital converter. Unit comes fully assembled as shown. Works from 2.7V up to 5.5V. Documents: Schematic Example PIC ADC Code OPA344 Datasheet Example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
  Generic male header - 5 pins: Generic male header
