# Fritzing sketch HomeAtion_RemoteLedEnv_Breadboard (saved by Fritzing 0.8.7b)
breadboards: 1

parts:
  AT328 = atmega328 [package=dip]
  C1 = Ceramic Capacitor [capacitance=100nF package="100 mil [THT, multilayer]"]
  C2 = Electrolytic Capacitor [capacitance=2.2µF package="100 mil [THT, electrolytic]"]
  C3 = Ceramic Capacitor [capacitance=100nF package="100 mil [THT, multilayer]"]
  S2 = Pushbutton [package="[THT]"]
  R2 = Resistor [tolerance=±5% resistance=4.7k package=THT]
  LDO_3_3V1 = V_REG_LD1117VXX [package=78xxl]
  C4 = Electrolytic Capacitor [capacitance=2.2µF package="100 mil [THT, electrolytic]"]
  C5 = Ceramic Capacitor [capacitance=100nF package="100 mil [THT, multilayer]"]
  SW2 = DIP SWITCH [package=dipswitch-02]
  LED2 = LED - 5mm [color="Red (633nm)" package="5 mm [THT]"]
  R3 = Resistor [tolerance=±5% resistance=1k package=THT]
  J3 = female pin header, 4 pins [form="♀ (female)"]
  J2 = female pin header, 4 pins [form="♀ (female)"]
  Ethernet_Module1 = shrouded pin header, 6 pins [form="♂ (shrouded male)"]
  J9 = male pin header, 5 pins [form="♂ (male)"]

nets:
  N1: AT328.RESET, S2.Pin_1, S2.Pin_2, R2.Pin_0
  N2: AT328.D4, Ethernet_Module1.pin6
  N3: AT328.VCC, AT328.AVCC, C1.0, C2.+, C3.1, R2.Pin_1, LDO_3_3V1.IN, C5.0, Ethernet_Module1.pin4
  GND: AT328.GND, C1.1, C2.-, S2.Pin_3, S2.Pin_4, LDO_3_3V1.GND, C4.-, C5.1, R3.Pin_1, J3.pin4, J9.pin5
  N4: AT328.D5_(PWM), Ethernet_Module1.pin5
  N5: AT328.D6_(PWM), Ethernet_Module1.pin3
  N6: AT328.D7, Ethernet_Module1.pin2
  N7: AT328.D8, Ethernet_Module1.pin1
  N8: AT328.D9_(PWM), J3.pin3
  N9: AT328.D10_(PWM), J2.pin3
  N10: AT328.D11_(PWM), J2.pin2
  N11: AT328.D12, J3.pin1
  N12: AT328.D13, J3.pin2
  N13: LDO_3_3V1.OUT, C4.+, SW2.3
  N14: SW2.1, J9.pin1
  N15: SW2.2, J2.pin4
  N16: SW2.4, LED2.anode
  N17: LED2.cathode, R3.Pin_0

custom parts:
  V_REG_LD1117VXX: LD1117VXX voltage regulator. We carry the 3.3V version (COM-00526) in TO-220 package.
