# Fritzing sketch HomeAtion_RemoteLedEnv_Breadboard_Schematic (saved by Fritzing 0.9.2b)

parts:
  Part1 = Arduino Pro Mini v13
  NRF24L1 = NRF24L01
  DHT1 = DHT11 Humitidy and Temperature Sensor
  Part2 = Breakout Board for Electret Microphone
  Part3 = ws2812b [package="smd 2812b"]
  Power_+5V = Generic male header - 5 pins [form="♂ (male)" package=THT]

nets:
  3.3V: Part1.VCC, NRF24L1.VCC, Part2.VCC
  GND: Part1.GND, NRF24L1.GND, DHT1.GND, Part2.GND, Part3.VSS, Power_+5V.GND
  5V: Part1.RAW, DHT1.VDD, Part3.VDD, Power_+5V.VCC
  N1: Part1.A0, Part2.OUT
  N2: Part1.D13/SCK, NRF24L1.SCK
  N3: Part1.D12/MISO, NRF24L1.MISO
  N4: Part1.D11_PWM/MOSI, NRF24L1.MOSI
  N5: Part1.D10_PWM/SS, NRF24L1.CSN
  N6: Part1.D9_PWM, NRF24L1.CE
  N7: Part1.D6_PWM, Part3.DIN
  N8: Part1.D2, DHT1.DATA

custom parts:
  NRF24L01: NRF24L01 module
  DHT11 Humitidy and Temperature Sensor: DHT11 Humidity and Temperature Sensor
  Breakout Board for Electret Microphone: Description: Ready to add audio to your next project? This small breakout board couples a small electret microphone with a 100x opamp to amplify the sounds of voice, door knocks, etc loud enough to be picked up by a microcontroller's Analog to Digital converter. Unit comes fully assembled as shown. Works from 2.7V up to 5.5V. Documents: Schematic Example PIC ADC Code OPA344 Datasheet Example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
  Generic male header - 5 pins: Generic male header
