# Fritzing sketch HomeAtion_RemoteLedEnv_Schematic (saved by Fritzing 0.8.7b)
breadboards: 1
perfboards: 1

parts:
  AT328 = atmega328 [package=dip]
  C1 = Ceramic Capacitor [capacitance=100nF package="100 mil [THT, multilayer]"]
  C2 = Electrolytic Capacitor [capacitance=2.2µF package="100 mil [THT, electrolytic]"]
  C3 = Ceramic Capacitor [capacitance=100nF package="100 mil [THT, multilayer]"]
  RESET = Pushbutton [package="[THT]"]
  R2 = Resistor [tolerance=±5% resistance=4.7k package=THT]
  LDO_3_3V = V_REG_LD1117VXX [package=78xxl]
  C4 = Electrolytic Capacitor [capacitance=2.2µF package="100 mil [THT, electrolytic]"]
  C5 = Ceramic Capacitor [capacitance=100nF package="100 mil [THT, multilayer]"]
  Main_switch = DIP SWITCH [package=dipswitch-02]
  R3 = Resistor [tolerance=±5% resistance=1k package=THT]
  Relay = shrouded pin header, 6 pins [form="♂ (shrouded male)"]
  NRF24 = double row female pin header, 8 pins [form="♀ (female)"]
  LED_Power = LED - 3mm [color="Red (633nm)" package="3 mm [THT]"]

nets:
  5V: AT328.RESET, AT328.VCC, AT328.AVCC, C1.0, C2.+, C3.1, RESET.Pin_1, RESET.Pin_2, R2.Pin_0, R2.Pin_1, Main_switch.2, Relay.pin6
  GND: AT328.GND, C1.1, C2.-, C3.0, RESET.Pin_3, RESET.Pin_4, LDO_3_3V.GND, C4.-, C5.1, R3.Pin_1, Relay.pin1, NRF24.pin1
  N1: AT328.D5_(PWM), Relay.pin2
  N2: AT328.D6_(PWM), Relay.pin3
  N3: AT328.D7, Relay.pin4
  N4: AT328.D8, Relay.pin5
  N5: AT328.D9_(PWM), NRF24.pin3
  N6: AT328.D10_(PWM), NRF24.pin4
  N7: AT328.D11_(PWM), NRF24.pin6
  N8: AT328.D12, NRF24.pin7
  N9: AT328.D13, NRF24.pin5
  Power3V3: LDO_3_3V.OUT, C4.+, Main_switch.4
  Power5V: LDO_3_3V.IN, C5.0, Main_switch.3, LED_Power.anode
  3.3V: Main_switch.1, NRF24.pin2
  N10: R3.Pin_0, LED_Power.cathode

custom parts:
  V_REG_LD1117VXX: LD1117VXX voltage regulator. We carry the 3.3V version (COM-00526) in TO-220 package.
